// Logisim project s4698512-logisim.circ as structural Verilog: 1 circuit, main circuit main
module main (
  input  S
);

  wire and_1_out, and_2_out, and_3_out, and_4_out, and_5_out, and_6_out, and_7_out, and_8_out, and_9_out,
       CLK_out, F0_q, F0_qn, F1_q, F1_qn, F2_q, F2_qn, not_1_out, or_1_out, or_2_out, or_3_out, or_4_out,
       or_5_out, or_6_out, xnor_1_out, xor_1_out, xor_2_out;

  Clock CLK (.out(CLK_out));
  not not_1 (not_1_out, S);
  or or_1 (or_1_out, F0_q, not_1_out);
  and and_1 (and_1_out, F1_q, F2_qn, or_1_out);
  and and_2 (and_2_out, F1_qn, F0_qn, S);
  xnor xnor_1 (xnor_1_out, F0_q, S);
  and and_3 (and_3_out, F2_q, xnor_1_out);
  or or_2 (or_2_out, and_1_out, and_2_out, and_3_out);
  D_Flip_Flop F2 (.clk(CLK_out), .D(or_2_out), .Q(F2_q), .Qn(F2_qn));  // open: preset, en, reset
  xor xor_1 (xor_1_out, F1_q, F0_q);
  and and_4 (and_4_out, xor_1_out, S);
  D_Flip_Flop F1 (.clk(CLK_out), .D(and_4_out), .Q(F1_q), .Qn(F1_qn));  // open: preset, en, reset
  or or_3 (or_3_out, F0_qn, not_1_out);
  and and_5 (and_5_out, F1_q, or_3_out);
  and and_6 (and_6_out, F1_qn, not_1_out);
  or or_4 (or_4_out, and_5_out, and_6_out);
  D_Flip_Flop F0 (.clk(CLK_out), .D(or_4_out), .Q(F0_q), .Qn(F0_qn));  // open: preset, en, reset
  xor xor_2 (xor_2_out, F1_q, F0_q);
  and and_7 (and_7_out, F2_qn, F0_q);
  and and_8 (and_8_out, F2_q, xor_2_out);
  or or_5 (or_5_out, F0_qn, F2_qn);
  or or_6 (or_6_out, and_7_out, and_8_out);
  and and_9 (and_9_out, F1_q, or_5_out);
  LED X1 (.in(and_9_out));
  LED X0 (.in(or_6_out));

  // Notes on the sheet:
  //   Q2'
  //   Q2
  //   Q1'
  //   Q1
  //   Q0'
  //   Q0
endmodule
