// Logisim project Shift Register.circ as structural Verilog: 1 circuit, main circuit main
module main (
  input  in_1,
  input  in_2,
  input  in_3,
  input  in_4,
  input  Select,
  input  Right_shift_in,
  input  Right_Shift_In_2,
  input  Direction_Selection
);

  wire clock_1_out, clock_2_out, d_ff_1_q, d_ff_2_q, d_ff_3_q, d_ff_4_q, d_ff_5_q, d_ff_6_q,
       multiplexer_1_out, multiplexer_2_out, multiplexer_3_out, multiplexer_4_out, multiplexer_5_out,
       multiplexer_6_out;

  Clock clock_1 (.out(clock_1_out));
  Clock clock_2 (.out(clock_2_out));
  Multiplexer multiplexer_1 (.in0(in_1), .in1(in_4), .out(multiplexer_1_out), .sel(Select));  // open: en
  Multiplexer multiplexer_2 (
    .in0(d_ff_4_q), .in1(Right_Shift_In_2), .out(multiplexer_2_out), .sel(Direction_Selection));  // open: en
  D_Flip_Flop d_ff_1 (.clk(clock_2_out), .D(multiplexer_1_out), .Q(d_ff_1_q));  // open: Qn, preset, en, reset
  LED led_1 (.in(d_ff_1_q));
  D_Flip_Flop d_ff_2 (.clk(clock_1_out), .D(multiplexer_2_out), .Q(d_ff_2_q));  // open: Qn, preset, en, reset
  LED led_2 (.in(d_ff_2_q));
  Multiplexer multiplexer_3 (.in0(in_2), .in1(d_ff_1_q), .out(multiplexer_3_out), .sel(Select));  // open: en
  Multiplexer multiplexer_4 (
    .in0(d_ff_5_q), .in1(d_ff_2_q), .out(multiplexer_4_out), .sel(Direction_Selection));  // open: en
  D_Flip_Flop d_ff_3 (.clk(clock_2_out), .D(multiplexer_3_out), .Q(d_ff_3_q));  // open: Qn, preset, en, reset
  LED led_3 (.in(d_ff_3_q));
  D_Flip_Flop d_ff_4 (.clk(clock_1_out), .D(multiplexer_4_out), .Q(d_ff_4_q));  // open: Qn, preset, en, reset
  Multiplexer multiplexer_5 (
    .in0(Right_shift_in), .in1(d_ff_4_q), .out(multiplexer_5_out), .sel(Direction_Selection));  // open: en
  LED led_4 (.in(d_ff_4_q));
  Multiplexer multiplexer_6 (.in0(in_3), .in1(d_ff_3_q), .out(multiplexer_6_out), .sel(Select));  // open: en
  D_Flip_Flop d_ff_5 (.clk(clock_1_out), .D(multiplexer_5_out), .Q(d_ff_5_q));  // open: Qn, preset, en, reset
  LED led_5 (.in(d_ff_5_q));
  D_Flip_Flop d_ff_6 (.clk(clock_2_out), .D(multiplexer_6_out), .Q(d_ff_6_q));  // open: Qn, preset, en, reset
  LED led_6 (.in(d_ff_6_q));
  LED led_7 (.in(d_ff_5_q));
  LED led_8 (.in(d_ff_6_q));

  // Notes on the sheet:
  //   One way
  //   Bidirectional
endmodule
