// Logisim project Universal Shift Register.circ as structural Verilog: 1 circuit, main circuit main
module main (
  input  in_1,
  input  in_2,
  input  in_3,
  input  Left_Shift_In,
  input  Right_Shift_In,
  input  Fn1,
  input  Fn0
);

  wire clock_1_out, d_ff_1_q, d_ff_2_q, d_ff_3_q, multiplexer_1_out, multiplexer_2_out, multiplexer_3_out;

  Clock clock_1 (.out(clock_1_out));
  Multiplexer #(.select(2)) multiplexer_1 (
    .in0(in_1), .in1(d_ff_2_q), .in2(Right_Shift_In), .in3(d_ff_1_q), .out(multiplexer_1_out),
    .sel({Fn0, Fn1}));  // open: en
  D_Flip_Flop d_ff_1 (.clk(clock_1_out), .D(multiplexer_1_out), .Q(d_ff_1_q));  // open: Qn, preset, en, reset
  LED led_1 (.in(d_ff_1_q));
  Multiplexer #(.select(2)) multiplexer_2 (
    .in0(in_2), .in1(d_ff_3_q), .in2(d_ff_1_q), .in3(d_ff_2_q), .out(multiplexer_2_out), .sel({Fn0, Fn1}));  // open: en
  D_Flip_Flop d_ff_2 (.clk(clock_1_out), .D(multiplexer_2_out), .Q(d_ff_2_q));  // open: Qn, preset, en, reset
  LED led_2 (.in(d_ff_2_q));
  Multiplexer #(.select(2)) multiplexer_3 (
    .in0(in_3), .in1(Left_Shift_In), .in2(d_ff_2_q), .in3(d_ff_3_q), .out(multiplexer_3_out), .sel({Fn0, Fn1}));  // open: en
  D_Flip_Flop d_ff_3 (.clk(clock_1_out), .D(multiplexer_3_out), .Q(d_ff_3_q));  // open: Qn, preset, en, reset
  LED led_3 (.in(d_ff_3_q));

  // Notes on the sheet:
  //   Universal Shift Register (3-bit)
endmodule
