// Logisim project Test Help.circ as structural Verilog: 1 circuit, main circuit main
module main (
  input  in_1,
  input  in_2,
  input  in_3,
  input  in_4,
  input  INVB,
  input  ENB,
  input  B,
  input  INVA,
  input  ENA,
  input  A,
  input  F2,
  input  F1,
  input  F0,
  input  in_14
);

  wire and_1_out, and_2_out, and_3_out, and_4_out, and_5_out, and_6_out, clock_1_out, d_ff_1_q, d_ff_2_q,
       multiplexer_1_out, multiplexer_2_out, multiplexer_3_out, nor_1_out, not_1_out, not_2_out, or_1_out,
       xor_1_out, xor_2_out, xor_3_out, xor_4_out, xor_5_out;

  Clock clock_1 (.out(clock_1_out));
  Multiplexer multiplexer_1 (.in0(in_2), .in1(d_ff_2_q), .out(multiplexer_1_out), .sel(in_3));  // open: en
  and and_1 (and_1_out, ENB, B);
  and and_2 (and_2_out, ENA, A);
  D_Flip_Flop d_ff_1 (.clk(clock_1_out), .D(multiplexer_1_out), .Q(d_ff_1_q));  // open: Qn, preset, en, reset
  xor xor_1 (xor_1_out, INVB, and_1_out);
  xor xor_2 (xor_2_out, INVA, and_2_out);
  LED led_1 (.in(d_ff_1_q));
  LED led_2 (.in(xor_2_out));
  and and_3 (and_3_out, xor_1_out, xor_2_out);
  Multiplexer multiplexer_2 (.in0(in_1), .in1(d_ff_1_q), .out(multiplexer_2_out), .sel(in_3));  // open: en
  and and_4 (and_4_out, xor_2_out, xor_1_out);
  and and_5 (and_5_out, xor_2_out, xor_1_out);
  xor xor_3 (xor_3_out, xor_2_out, xor_1_out);
  nor nor_1 (nor_1_out, xor_2_out, xor_1_out);
  not not_1 (not_1_out, xor_2_out);
  xor xor_4 (xor_4_out, xor_2_out, xor_1_out);
  D_Flip_Flop d_ff_2 (.clk(clock_1_out), .D(multiplexer_2_out), .Q(d_ff_2_q));  // open: Qn, preset, en, reset
  not not_2 (not_2_out, and_4_out);
  and and_6 (and_6_out, F0, xor_4_out, in_4);
  or or_1 (or_1_out, and_3_out, and_6_out);
  LED led_3 (.in(or_1_out));
  LED led_4 (.in(d_ff_2_q));
  Multiplexer #(.select(3), .enable("false")) multiplexer_3 (
    .in0(not_2_out), .in1(and_5_out), .in2(xor_3_out), .in3(nor_1_out), .in4(in_4), .in5(not_1_out),
    .in6(in_14), .in7(xor_5_out), .out(multiplexer_3_out), .sel({F2, F1, F0}));
  xor xor_5 (xor_5_out, in_4, xor_4_out);
  LED led_5 (.in(multiplexer_3_out));

  // Notes on the sheet:
  //   Right shift out
  //   Right Shift in
  //   Carry in
  //   Carry Out
  //   Output
endmodule
