// Logisim project Circuit 2.circ as structural Verilog: 1 circuit, main circuit main
module main (
  input  A0,
  input  A1
);

  wire and_1_out, and_2_out, and_3_out, and_4_out, not_1_out, not_2_out;

  not not_1 (not_1_out, A0);
  not not_2 (not_2_out, A1);
  and and_1 (and_1_out, not_1_out, not_2_out);
  and and_2 (and_2_out, not_1_out, A1);
  and and_3 (and_3_out, A0, not_2_out);
  and and_4 (and_4_out, A0, A1);
  LED led_1 (.in(and_1_out));
  LED led_2 (.in(and_2_out));
  LED led_3 (.in(and_3_out));
  LED led_4 (.in(and_4_out));

  // Notes on the sheet:
  //   A0_ A1_
  //   A1
  //   A0
  //   A0'
  //   A1'
endmodule
