// Logisim project Circuit 3.circ as structural Verilog: 1 circuit, main circuit main
module main (
  input  A0,
  input  A1,
  input  A2,
  input  A3,
  input  B0,
  input  B1,
  input  B2,
  input  B3,
  input  M
);

  wire adder_1_cout;
  wire [3:0] adder_1_out, multiplexer_1_out, not_1_out;

  not not_1 (not_1_out[0], B0);
  not not_2 (not_1_out[1], B1);
  not not_3 (not_1_out[2], B2);
  not not_4 (not_1_out[3], B3);
  Multiplexer #(.width(4)) multiplexer_1 (
    .in0({B3, B2, B1, B0}), .in1(not_1_out), .out(multiplexer_1_out), .sel(M));  // open: en
  Adder #(.width(4)) adder_1 (
    .a({A3, A2, A1, A0}), .b(multiplexer_1_out), .out(adder_1_out), .cin(M), .cout(adder_1_cout));
  LED led_1 (.in(adder_1_cout));
  LED led_2 (.in(adder_1_out[0]));
  LED led_3 (.in(adder_1_out[1]));
  LED led_4 (.in(adder_1_out[2]));
  LED led_5 (.in(adder_1_out[3]));
endmodule
