// Logisim project Circuit 6.circ as structural Verilog: 1 circuit, main circuit main
module main (
  input  in_1,
  input  in_2,
  input  in_3,
  input  in_4
);

  wire clock_1_out, d_ff_1_q, d_ff_1_qn;

  Clock clock_1 (.out(clock_1_out));
  D_Flip_Flop d_ff_1 (
    .clk(clock_1_out), .D(in_1), .Q(d_ff_1_q), .Qn(d_ff_1_qn), .preset(in_2), .en(in_3), .reset(in_4));
  LED led_1 (.in(d_ff_1_q));
  LED led_2 (.in(d_ff_1_qn));
endmodule
