// Logisim project 3-bit Synchronous Counter.circ as structural Verilog: 1 circuit, main circuit main
module main (
);

  wire clock_1_out, d_ff_1_q, d_ff_1_qn, d_ff_2_q, d_ff_3_q, Set_to_000_out, Set_to_111_out, xnor_1_out,
       xor_1_out;

  Clock clock_1 (.out(clock_1_out));
  Button Set_to_111 (.out(Set_to_111_out));
  Button Set_to_000 (.out(Set_to_000_out));
  LED led_1 (.in(d_ff_1_q));
  D_Flip_Flop d_ff_1 (
    .clk(clock_1_out), .D(xnor_1_out), .Q(d_ff_1_q), .Qn(d_ff_1_qn), .preset(Set_to_111_out),
    .reset(Set_to_000_out));  // open: en
  xnor xnor_1 (xnor_1_out, d_ff_2_q, d_ff_3_q);
  LED led_2 (.in(d_ff_2_q));
  D_Flip_Flop d_ff_2 (
    .clk(clock_1_out), .D(d_ff_1_qn), .Q(d_ff_2_q), .preset(Set_to_111_out), .reset(Set_to_000_out));  // open: Qn, en
  xor xor_1 (xor_1_out, d_ff_1_q, d_ff_3_q);
  LED led_3 (.in(d_ff_3_q));
  D_Flip_Flop d_ff_3 (
    .clk(clock_1_out), .D(xor_1_out), .Q(d_ff_3_q), .preset(Set_to_111_out), .reset(Set_to_000_out));  // open: Qn, en

  // Notes on the sheet:
  //   Last digit of 8-digit student number
  //   46985123 ---> 3
  //   Count sequence: 
  //   111 100 101 000 110 001 011 111
endmodule
