// Logisim project 4-bit up-down counter.circ as structural Verilog: 1 circuit, main circuit main
module main (
  input  [3:0] in_1,
  input  [3:0] _1,
  input  Add_Subtract,
  output [3:0] out_4
);

  wire clock_1_out;
  wire [3:0] adder_1_out, multiplexer_1_out;

  Multiplexer #(.width(4)) multiplexer_1 (
    .in0(in_1), .in1(_1), .out(multiplexer_1_out), .sel(Add_Subtract));  // open: en
  Adder #(.width(4)) adder_1 (.a(out_4), .b(multiplexer_1_out), .out(adder_1_out));  // open: cin, cout
  Clock clock_1 (.out(clock_1_out));
  Register #(.width(4)) register_1 (.D(adder_1_out), .Q(out_4), .clk(clock_1_out));  // open: en, clr
  LED led_1 (.in(out_4[3]));
  LED led_2 (.in(out_4[2]));
  LED led_3 (.in(out_4[1]));
  LED led_4 (.in(out_4[0]));
endmodule
