// Logisim project Combinational Lock.circ as structural Verilog: 1 circuit, main circuit main
module main (
  input  in_1,
  input  in_2,
  input  in_3,
  input  in_4
);

  wire and_1_out, and_2_out, and_3_out, clock_1_out, d_ff_1_q, d_ff_2_q, d_ff_3_q, d_ff_4_q, d_ff_5_q,
       d_ff_6_q, d_ff_7_q, d_ff_8_q, not_1_out, not_2_out, not_3_out, not_4_out, not_5_out, not_6_out;

  Clock clock_1 (.out(clock_1_out));
  D_Flip_Flop d_ff_1 (.clk(clock_1_out), .D(in_1), .Q(d_ff_1_q));  // open: Qn, preset, en, reset
  D_Flip_Flop d_ff_2 (.clk(clock_1_out), .D(in_2), .Q(d_ff_2_q));  // open: Qn, preset, en, reset
  D_Flip_Flop d_ff_3 (.clk(clock_1_out), .D(in_3), .Q(d_ff_3_q));  // open: Qn, preset, en, reset
  D_Flip_Flop d_ff_4 (.clk(clock_1_out), .D(in_4), .Q(d_ff_4_q));  // open: Qn, preset, en, reset
  not not_1 (not_1_out, d_ff_2_q);
  not not_2 (not_2_out, d_ff_1_q);
  and and_1 (and_1_out, not_2_out, not_1_out, d_ff_3_q, d_ff_4_q);
  D_Flip_Flop d_ff_5 (.clk(clock_1_out), .D(d_ff_1_q), .Q(d_ff_5_q));  // open: Qn, preset, en, reset
  D_Flip_Flop d_ff_6 (.clk(clock_1_out), .D(d_ff_2_q), .Q(d_ff_6_q));  // open: Qn, preset, en, reset
  D_Flip_Flop d_ff_7 (.clk(clock_1_out), .D(d_ff_3_q), .Q(d_ff_7_q));  // open: Qn, preset, en, reset
  D_Flip_Flop d_ff_8 (.clk(clock_1_out), .D(d_ff_4_q), .Q(d_ff_8_q));  // open: Qn, preset, en, reset
  and and_2 (and_2_out, and_3_out, and_1_out);
  not not_3 (not_3_out, d_ff_6_q);
  not not_4 (not_4_out, d_ff_5_q);
  and and_3 (and_3_out, not_4_out, not_3_out, d_ff_7_q, not_5_out);
  not not_5 (not_5_out, d_ff_8_q);
  not not_6 (not_6_out, and_2_out);
  LED Unlocked (.in(and_2_out));
  LED Locked (.in(not_6_out));

  // Notes on the sheet:
  //   0011
  //   0010
endmodule
