// Logisim project ClockDemo.circ as structural Verilog: 2 circuits, main circuit Clock
module Clock (
  input  \复位 ,
  input  \时钟输入使能 ,
  input  \时钟选择_1为内部时钟_0为外部时钟 ,
  output out_4,
  output out_5,
  output out_6,
  output out_7,
  output out_8,
  output out_9
);

  wire \clk_1_内部时钟输出 , \时钟输入_out ;

  Button \u_时钟输入  (.out(\时钟输入_out ));
  clk clk_1 (
    .\ET_时钟产生使能 (\时钟输入使能 ), .\QD_产生时钟_接一个按键 (\时钟输入_out ), .\复位 (\复位 ), .W2(out_9), .W1(out_8),
    .\内部时钟输出 (\clk_1_内部时钟输出 ), .\T2_时钟第三节拍 (out_5), .\T1_时钟第二节拍 (out_6), .\T0_时钟第一节拍 (out_7),
    .\时钟选择_1_内部晶振时钟_0_外部接入时钟 (\时钟选择_1为内部时钟_0为外部时钟 ));
  Multiplexer multiplexer_1 (
    .in0(\时钟输入_out ), .in1(\clk_1_内部时钟输出 ), .out(out_4), .sel(\时钟选择_1为内部时钟_0为外部时钟 ));  // open: en

  // Other names for the same wires on the sheet: clk = out_4; T0 = out_7; T1 = out_6; T2 = out_5; W1 = out_8;
  //   W2 = out_9
endmodule

// CLK
module clk (
  input  \ET_时钟产生使能 ,
  input  \QD_产生时钟_接一个按键 ,
  input  \时钟选择_1_内部晶振时钟_0_外部接入时钟 ,
  input  \复位 ,
  output W1,
  output W2,
  output \T1_时钟第二节拍 ,
  output \T0_时钟第一节拍 ,
  output \T2_时钟第三节拍 ,
  output \内部时钟输出 
);

  wire and_1_out, clock_1_out, counter_2_q, multiplexer_1_out;
  wire [1:0] counter_1_q;

  and and_1 (and_1_out, \ET_时钟产生使能 , \时钟选择_1_内部晶振时钟_0_外部接入时钟 );
  Clock_part clock_1 (.out(clock_1_out));
  assign \内部时钟输出  = and_1_out ? clock_1_out : 1'bz;  // Controlled_Buffer controlled_buffer_1
  Counter #(.width(2), .max('h2)) counter_1 (
    .load(1'b0), .count(1'b1), .Q(counter_1_q), .clk(multiplexer_1_out), .clr(\复位 ));  // open: D, carry
  Multiplexer multiplexer_1 (
    .in0(\QD_产生时钟_接一个按键 ), .in1(clock_1_out), .out(multiplexer_1_out), .sel(and_1_out));  // open: en
  Decoder #(.select(2)) decoder_1 (
    .out0(\T2_时钟第三节拍 ), .out1(\T0_时钟第一节拍 ), .out2(\T1_时钟第二节拍 ), .sel(counter_1_q), .en(\ET_时钟产生使能 ));  // open: out3
  Counter #(.width(1), .max('h1)) counter_2 (
    .D(\ET_时钟产生使能 ), .Q(counter_2_q), .clk(\T0_时钟第一节拍 ), .clr(\复位 ));  // open: load, count, carry
  Decoder decoder_2 (.out0(W2), .out1(W1), .sel(counter_2_q), .en(\ET_时钟产生使能 ));

  // Notes on the sheet:
  //   ET_时钟产生使能: pull=down
endmodule
